// Digital circuit Counter16.dig as structural Verilog
module Counter16 (
  input  nUp,
  input  nDn,
  input  [15:0] In,
  input  nLd,
  input  Clr,
  output [15:0] Out,
  output nBO
);

  wire _74193_1_p11, _74193_1_p12, _74193_2_p11, _74193_2_p12, _74193_3_p11, _74193_3_p12;

  // _74193 _74193_1: pin names not known; wires that end beside it: In[0], nDn, nUp, In[1], In[2], In[3], Clr, nLd, 1'b1, 1'b0, _74193_1_p11, _74193_1_p12, Out[0], Out[1], Out[2], Out[3]
  // _74193 _74193_2: pin names not known; wires that end beside it: In[4], _74193_1_p11, _74193_1_p12, In[5], In[6], In[7], Clr, nLd, 1'b1, 1'b0, _74193_2_p11, _74193_2_p12, Out[4], Out[5], Out[6], Out[7]
  // _74193 _74193_3: pin names not known; wires that end beside it: In[8], _74193_2_p11, _74193_2_p12, In[9], In[10], In[11], Clr, nLd, 1'b1, 1'b0, _74193_3_p11, _74193_3_p12, Out[8], Out[9], Out[10], Out[11]
  // _74193 _74193_4: pin names not known; wires that end beside it: In[12], _74193_3_p11, _74193_3_p12, In[13], In[14], In[15], Clr, nLd, 1'b1, 1'b0, nBO, Out[12], Out[13], Out[14], Out[15]
endmodule
