// Digital circuit Director.dig as structural Verilog
module Director (
  input  En,
  input  Clk,
  input  Dir,
  output Up,
  output Dn
);

  wire and_1_out, not_1_out;

  and and_1 (and_1_out, En, Clk);
  not not_1 (not_1_out, Dir);
  nand nand_1 (Up, and_1_out, not_1_out);
  nand nand_2 (Dn, and_1_out, Dir);
endmodule
